// Logisim project cpu.circ as structural Verilog: 3 circuits, main circuit CPU
module CPU (
  input  [31:0] Instruction,
  input  CLK,
  output [31:0] s0,
  output [31:0] s1,
  output [31:0] t0,
  output [31:0] t1,
  output [31:0] a0,
  output [31:0] ra,
  output [31:0] sp,
  output [31:0] PC
);

  wire main_1_p1;
  wire [4:0] undriven, undriven_2;
  wire [15:0] incrementer_1_p1, incrementer_1_p1_2;
  wire [31:0] alu_1_out, incrementer_1_p2, main_1_p5, multiplexer_1_out, multiplexer_2_out, regfile_1_r1,
       regfile_1_r2, rom_1_data;

  // Incrementer incrementer_1: pin names not known; wires that end beside it: {incrementer_1_p1_2, incrementer_1_p1}, incrementer_1_p2
  Multiplexer #(.width(32)) multiplexer_1 (
    .in0(incrementer_1_p2), .in1(alu_1_out), .out(multiplexer_1_out));  // open: sel, en
  // PC pc_1: pin names not known; wires that end beside it: multiplexer_1_out, CLK, {incrementer_1_p1_2, incrementer_1_p1}
  RAM #(.addrWidth(16), .dataWidth(32)) ram_1 ();  // open: addr, data, sel, clk, ld, clr
  ROM #(.addrWidth(16), .dataWidth(32)) rom_1 (.addr(incrementer_1_p1), .data(rom_1_data));  // open: sel
  ROM #(.addrWidth(16), .dataWidth(32)) rom_2 (.addr(incrementer_1_p1_2), .data(rom_1_data));  // open: sel
  Branch branch_1 ();  // open: A, in_6, in_1, in_2, in_3, in_4, out_7
  Multiplexer #(.width(32), .enable("false")) multiplexer_2 (
    .in0({incrementer_1_p1_2, incrementer_1_p1}), .in1(regfile_1_r1), .out(multiplexer_2_out));  // open: sel
  RegFile regfile_1 (
    .Clk(CLK), .R1(regfile_1_r1), .R2(regfile_1_r2), .W(rom_1_data), .RS1(undriven), .RS2(undriven_2),
    .s0(s0), .s1(s1), .t0(t0), .t1(t1), .a0(a0), .ra(ra), .sp(sp));  // open: WE, RD
  ALU alu_1 (.A(multiplexer_2_out), .B(regfile_1_r2), .Out(alu_1_out));  // open: ALU_Op, in_4
  // memory_main main_1: pin names not known; wires that end beside it: main_1_p1, main_1_p1, CLK, alu_1_out, main_1_p5
  Multiplexer #(.select(2), .width(32)) multiplexer_3 (
    .in0({incrementer_1_p1_2, incrementer_1_p1}), .in1(alu_1_out), .in2(alu_1_out), .out(main_1_p5));  // open: in3, sel, en

  // Other names for the same wires on the sheet: fetch_addr[31:0] = PC; INST[31:0] = Instruction

  // Notes on the sheet:
  //   NOTE
  //   Please do not modify/replace/move/change/delete/etc input and output pins
  //   These are debug/test outputs from your circuit
endmodule

module Branch (
  input  in_1,
  input  in_2,
  input  in_3,
  input  [1:0] in_4,
  input  [5:0] A,
  input  [5:0] in_6,
  output [1:0] out_7
);

  wire comparator_1_lt, comparator_2_lt, comparator_3_eq, multiplexer_1_out, multiplexer_2_out, not_1_out;
  wire [1:0] multiplexer_3_out;
  wire [31:6] B, undriven;

  Comparator #(.width(32)) comparator_1 (
    .a({undriven, A}), .b({B, A[5], in_6[4:0]}), .lt(comparator_1_lt));  // open: gt, eq
  Comparator #(.width(6), .mode("unsigned")) comparator_2 (
    .a(A), .b({A[5], in_6[4:0]}), .lt(comparator_2_lt));  // open: gt, eq
  Comparator #(.width(32)) comparator_3 (
    .a({undriven, A}), .b({B, A[5], in_6[4:0]}), .eq(comparator_3_eq));  // open: gt, lt
  Multiplexer #(.enable("false")) multiplexer_1 (
    .in0(comparator_1_lt), .in1(comparator_2_lt), .out(multiplexer_1_out), .sel(in_1));
  Multiplexer #(.enable("false")) multiplexer_2 (
    .in0(multiplexer_1_out), .in1(comparator_3_eq), .out(multiplexer_2_out), .sel(in_2));
  Multiplexer #(.enable("false")) multiplexer_3 (
    .in0(multiplexer_2_out), .in1(not_1_out), .out(multiplexer_3_out[0]), .sel(in_3));
  not not_1 (not_1_out, multiplexer_2_out);
  Multiplexer #(.select(2), .width(2), .enable("false")) multiplexer_4 (
    .in2(multiplexer_3_out), .out(out_7), .sel(in_4));  // open: in0, in1, in3
  // Pins of 6 and 32 bits meet at {B, A[5], in_6[4:0]}
  // Pins of 6 and 32 bits meet at {undriven, A}
  // Pins of 1 and 2 bits meet at multiplexer_3_out

  assign in_6[5] = A[5];

  // Other names for the same wires on the sheet: B[5:0] = {A[5], in_6[4:0]}; bit6 = A[5]
endmodule

module control (
  input  [31:0] R,
  input  [6:0] in_2,
  input  [6:0] in_3,
  input  [6:0] in_4,
  input  [6:0] in_5,
  input  [6:0] in_6,
  input  [6:0] in_7,
  input  [6:0] in_8,
  input  [6:0] in_9,
  input  [6:0] in_10,
  input  [6:0] in_11,
  input  [6:0] in_12,
  input  [6:0] in_13,
  input  [6:0] in_14,
  input  [6:0] in_15,
  input  [6:0] in_16,
  input  [6:0] in_17
);

  wire comparator_1_eq, comparator_2_eq, comparator_3_eq, comparator_4_eq, comparator_5_eq, comparator_6_eq,
       comparator_7_eq, comparator_8_eq, comparator_9_eq, comparator_10_eq, comparator_11_eq,
       comparator_12_eq, comparator_13_eq, comparator_14_eq, comparator_15_eq, comparator_16_eq,
       decoder_1_out0, decoder_1_out1;
  wire [6:0] undriven;

  Comparator #(.width(7)) comparator_1 (.a(R[6:0]), .b(in_2), .eq(comparator_1_eq));  // open: gt, lt
  Comparator #(.width(7)) comparator_2 (.a(R[6:0]), .b(in_4), .eq(comparator_2_eq));  // open: gt, lt
  Comparator #(.width(7)) comparator_3 (.a(R[6:0]), .b(in_6), .eq(comparator_3_eq));  // open: gt, lt
  Comparator #(.width(7)) comparator_4 (.a(R[6:0]), .b(in_8), .eq(comparator_4_eq));  // open: gt, lt
  Comparator #(.width(7)) comparator_5 (.a(R[6:0]), .b(in_10), .eq(comparator_5_eq));  // open: gt, lt
  Comparator #(.width(7)) comparator_6 (.a(R[6:0]), .b(in_12), .eq(comparator_6_eq));  // open: gt, lt
  Comparator #(.width(7)) comparator_7 (.a(R[6:0]), .b(in_14), .eq(comparator_7_eq));  // open: gt, lt
  Comparator #(.width(7)) comparator_8 (.a(R[6:0]), .b(in_16), .eq(comparator_8_eq));  // open: gt, lt
  Decoder #(.enable("false")) decoder_1 (.out0(decoder_1_out0), .out1(decoder_1_out1), .sel(comparator_1_eq));
  Comparator #(.width(7)) comparator_9 (.a(undriven), .b(in_3), .eq(comparator_9_eq));  // open: gt, lt
  Comparator #(.width(7)) comparator_10 (.a(R[6:0]), .b(in_5), .eq(comparator_10_eq));  // open: gt, lt
  Comparator #(.width(7)) comparator_11 (.a(R[6:0]), .b(in_7), .eq(comparator_11_eq));  // open: gt, lt
  Comparator #(.width(7)) comparator_12 (.a(R[6:0]), .b(in_9), .eq(comparator_12_eq));  // open: gt, lt
  Comparator #(.width(7)) comparator_13 (.a(R[6:0]), .b(in_11), .eq(comparator_13_eq));  // open: gt, lt
  Comparator #(.width(7)) comparator_14 (.a(R[6:0]), .b(in_13), .eq(comparator_14_eq));  // open: gt, lt
  Comparator #(.width(7)) comparator_15 (.a(R[6:0]), .b(in_15), .eq(comparator_15_eq));  // open: gt, lt
  Comparator #(.width(7)) comparator_16 (.a(R[6:0]), .b(in_17), .eq(comparator_16_eq));  // open: gt, lt
  Multiplexer #(.select(3), .enable("false")) multiplexer_1 (
    .in0(comparator_9_eq), .in1(comparator_10_eq), .in2(comparator_11_eq), .in3(comparator_12_eq),
    .in4(comparator_13_eq), .in5(comparator_14_eq), .in6(comparator_15_eq), .in7(comparator_16_eq));  // open: out, sel

  // Other names for the same wires on the sheet: Opcode[6:0] = R[6:0]; funct3[2:0] = R[14:12]; funct7[6:0] = R[31:25]
endmodule
