// Logisim project regfile.circ as structural Verilog: 1 circuit, main circuit RegFile
module RegFile (
  input  [4:0] RD,
  input  [4:0] RS1,
  input  [4:0] RS2,
  input  [31:0] W,
  input  WE,
  input  Clk,
  output [31:0] s0,
  output [31:0] s1,
  output [31:0] t0,
  output [31:0] t1,
  output [31:0] a0,
  output [31:0] ra,
  output [31:0] sp,
  output [31:0] R1,
  output [31:0] R2
);

  wire demultiplexer_1_out0, demultiplexer_1_out1, demultiplexer_1_out2, demultiplexer_1_out5,
       demultiplexer_1_out6, demultiplexer_1_out8, demultiplexer_1_out9, demultiplexer_1_out10,
       demultiplexer_1_out11, undriven;
  wire [31:0] a1, register_8_q;

  Multiplexer #(.select(5), .width(32), .enable("false")) multiplexer_1 (
    .in0({32{1'b0}}), .in1(ra), .in2(sp), .in5(t0), .in6(t1), .in8(s0), .in9(s1), .in10(a0), .in11(a1),
    .out(R1), .sel(RS1));  // open: in3, in4, in7, in12, in13, in14, in15, in16, in17, in18, in19, in20, in21, in22, in23, in24, in25, in26, in27, in28, in29, in30, in31
  Multiplexer #(.select(5), .width(32), .enable("false")) multiplexer_2 (
    .in0({32{1'b0}}), .in1(ra), .in2(sp), .in5(t0), .in6(t1), .in8(s0), .in9(s1), .in10(a0), .in11(a1),
    .out(R2), .sel(RS2));  // open: in3, in4, in7, in12, in13, in14, in15, in16, in17, in18, in19, in20, in21, in22, in23, in24, in25, in26, in27, in28, in29, in30, in31
  Register #(.width(32)) register_1 (.D(W), .en(demultiplexer_1_out8), .Q(s0), .clk(Clk));  // open: clr
  Register #(.width(32)) register_2 (.D(W), .en(demultiplexer_1_out9), .Q(s1), .clk(Clk));  // open: clr
  Register #(.width(32)) register_3 (.D(W), .en(demultiplexer_1_out5), .Q(t0), .clk(Clk));  // open: clr
  Register #(.width(32)) register_4 (.D(W), .en(demultiplexer_1_out6), .Q(t1), .clk(Clk));  // open: clr
  Register #(.width(32)) register_5 (.D(W), .en(demultiplexer_1_out10), .Q(a0), .clk(Clk));  // open: clr
  Register #(.width(32)) register_6 (.D(W), .en(demultiplexer_1_out1), .Q(ra), .clk(Clk));  // open: clr
  Register #(.width(32)) register_7 (.D(W), .en(demultiplexer_1_out2), .Q(sp), .clk(Clk));  // open: clr
  Register #(.width(32)) register_8 (.D({32{1'b0}}), .en(undriven), .Q(register_8_q));  // open: clk, clr
  Register #(.width(32)) register_9 (.D(W), .en(demultiplexer_1_out11), .Q(a1), .clk(Clk));  // open: clr
  Demultiplexer #(.select(5), .enable("false")) demultiplexer_1 (
    .out0(demultiplexer_1_out0), .out1(demultiplexer_1_out1), .out2(demultiplexer_1_out2),
    .out5(demultiplexer_1_out5), .out6(demultiplexer_1_out6), .out8(demultiplexer_1_out8),
    .out9(demultiplexer_1_out9), .out10(demultiplexer_1_out10), .out11(demultiplexer_1_out11), .in(WE),
    .sel(RD));  // open: out3, out4, out7, out12, out13, out14, out15, out16, out17, out18, out19, out20, out21, out22, out23, out24, out25, out26, out27, out28, out29, out30, out31
  // also tied to GND on the sheet: demultiplexer_1_out0

  // Notes on the sheet:
  //   Write Register
  //   Read Register 1
  //   Read Register 2
  //   Write Data
  //   Write Enable
  //   Clock
  //   NOTE
  //   Please do not modify/replace/move/change/delete/etc input and output pins
  //   These are debug/test outputs from your circuit
  //   Read Data 1
  //   Read Data 2
endmodule
